# Fritzing sketch FanControl (saved by Fritzing 0.9.10b)

parts:
  Part1 = Arduino Nano (Rev3.0)
  Part2 = LCD1602-I2C
  DS1 = DS18B20 1-Wire Temperature Sensor [part_number=DS18B20]
  R1 = Resistor [tolerance=±5% power=0.25 resistance=4.7k package=THT]
  RE1 = KY-040 Rotary encoder [package=THT]
  F1 = Fan - 4 wire [package=THT]
  F2 = Fan - 4 wire [package=THT]
  J1 = Power Jack [package=power_jack_combo]  # not connected

nets:
  GND: Part1.GND, Part2.GND, DS1.GND, RE1.GND, F1.GND, F2.GND
  N1: Part1.D2, RE1.CLK
  N2: Part1.D3, RE1.DT
  N3: Part1.D4, RE1.SW
  N4: Part1.D5, F2.PWM
  N5: Part1.D6, F1.PWM
  N6: Part1.D7, DS1.DQ, R1.Pin_0
  N7: Part1.D8, F2.Tach
  N8: Part1.D9, F1.Tach
  5V: Part1.5V, DS1.VDD, R1.Pin_1, RE1.Vcc
  N9: Part1.A5, Part2.SCL
  N10: Part1.A4, Part2.SDA

custom parts:
  LCD1602-I2C: A standard character display, usually with 2x16 characters. Comes in many colors with LCM1602 IIC attached.
  KY-040 Rotary encoder: KY-040 Rotary Encoder with switch on breakout borad from AZ Delivery
  Fan - 4 wire: Fan, 4 wire with tach.
